// Logisim project Logisim.circ as structural Verilog: 8 circuits, main circuit main
module main (
);

  wire clock_1_out;

  ROM #(.addrWidth(16)) rom_1 ();  // open: addr, data
  Clock clock_1 (.out(clock_1_out));
  RAM #(.addrWidth(16)) ram_1 ();  // open: addr, we, oe, clk, din, dout

  // Notes on the sheet:
  //   contents of rom_1 (hex, n*v repeats v):
  //   256*0 f7 a5 59 b0 f3 db be 32 9f a4 3e 9a b9 e4 55 22 97 d2 73 ab 6c ee de d0 c9 32 d6 38 67 87 f9
  //   2c 23 7a e8 69 49 2f 2b 36 14 95 51 b7 75 db 5b 83 13 22 5a 75 93 73 57 bf 18 f2 72 44 d 54 4d 25 21
  //   8d aa 9c 93 ce 52 9 af ae 38 4a 97 a6 de 4f 46 c3 f8 ec d2 96 4e f1 f1 6e e6 77 bd c9 61 7c bb 6 a5
  //   b2 19 5f bc 93 36 17 fb b8 68 ef 66 6b f8 de 53 7a 71 0 4c 4e 1a cd 39 3b c0 8e be 18 b8 d e2 12 23
  //   8c f0 bd 73 f7 a1 6b 2e 5c 7a c1 f2 9a 73 86 b8 58 d9 be 5c 39 74 f7 5c 4d ec e2 df ca 68 24 f9 fb
  //   77 6e 2d 77 33 ca 32 96 a3 38 fa 21 61 79 ef 48 7c 2a 7f d8 9f 13 da ad 72 c0 fa 64 40 51 e3 55 d9
  //   8e 2c c0 b9 3e bd 45 69 b8 d9 99 24 ba 5e 76 be 79 4b d3 c1 f8 83 55 d9 9c d0 4 71 0 2a 41 9d 6 38
  //   f7 3a 2e 16 11 53 2a 58 2b c6 b1 4e 8b 26 93 89 52 e3 d 9e ee a8 5e 29 d2 4 99 14 69 4b bd 18 47 be
  //   2 84 a1 e9 75 3d ff 4c c6 5 2f 3d 60 ff 7c c ba 72 20 68 ec cd f6 0 85 ea 73 6d 9b 96 d7 4e 22 51 9f
  //   b4 81 51 3d c0 62 cd a 8b c9 77 7b 45 68 49 93 a0 30 84 98 6e 2b f5 9 88 88 7a ce f2 f7 c4 b1 3c 37
  //   5d c 2a ec ec c4 97 b5 b7 75 95 7e 6a ee d9 12 16 df 56 f3 7b d1 27 6d 8a 55 b1 e8 24 80 8 7e 28 96
  //   92 cd ac 4 e9 d 89 93 5 64 1d da 9a 78 4b f4 bf 46 c6 73 d0 32 8f 94 94 5e bb b3 a1 3e 79 1 fe 6b 53
  //   73 a b8 b4 fd 9d 83 a9 0 6c 4c eb 0 b1 8b 1d 99 b bd 51 b3 a2 bf d0 f4 8e 60 1a 76 79 31 2b b9 82 9e
  //   0 db 64 41 58 6 d7 75 bf 28 36 2a c7 e9 61 f8 98 da e4 75 ab e9 58 cb d2 1d 9 84 7b 7e d8 a7 34 54
  //   63 9 71 94 62 dc 8d 97 54 8b e d 5a ca 2d 30 61 e8 94 3c 87 67 69 1d b7 ce 8b 6a 95 bc 1a 92 a1 40
  //   3d 54 96 68 1e 74 13 17 39 ab 7d 1b d6 de 22 7e d3 93 a2 1c a7 a0 8a 76 a3 24 41 c4 79 bb 27 50 2 ec
  //   fa 1 3b e6 7c 35 90 6c 52 d4 5d c 2f a1 b1 96 31 d3 54 cc 8a e4 a 56 63 a8 19 f8 fc a0 9 6 17 8f aa
  //   16 96 4e 5b f7 63 dc 88 e2 8f b9 74 ef bd 73 38 ca c1 80 a a6 83 4e c2 70 29 98 9a 48 75 fb 35 2c 6a
  //   c9 e2 f6 35 1b 21 88 4b 2c 65 44 ce e5 1b c2 34 b3 eb bc 2a a0 3d 4d b5 a1 fe 5a 9b 2c a3 50 0 e 6d
  //   f 53 7a ee 25 6a 64 cc 3f eb f c5 db ee e5 f3 42 e0 86 50 b5 aa 22 7b e6 11 b bb a9 5f 85 44 eb 43
  //   e0 b9 e2 f5 c8 f2 86 9d db fe 3f f5 7c 6b df 2c e6 c4 d1 d 84 5a 93 60 7f 47 61 90 97 b0 32 8d 35 49
  //   e7 f3 c1 1d c2 6b 31 8f 14 51 e2 9b 3a 97 aa 61 c9 e8 2d e4 8 10 70 e 9e 9a ab f7 8c ba 62 66 5c 6d
  //   b6 97 9a de f8 3e 83 b 7e cb fc a8 ba f0 c5 43 87 60 ee a8 c6 d8 89 86 29 62 a0 52 4e d8 69 6b f a7
  //   b8 7e 18 d5 b4 2b b9 44 cd e8 fc 37 ed 25 fa 15 ed b1 6a 6d 4a 5c 7a 3a 18 dc e1 67 36 f4 34 94 c2
  //   d2 79 1a cf b8 f9 4c 55 df 5a 0 68 97 ec 4d ad b2 43 95 8 22 5 c5 9a e1 4 db ea 10 8e a8 61 63 4 d7
  //   fb bb a9 2d 3b 14 bb 11 60 a1 c7 4f d5 34 39 18 ed e3 32 4d cf e8 9e fc ae c9 84 2a 3d b8 9f d2 62
  //   3b 2e 2d 29 f 8 34 fb 4a f2 62 e bf 34 be 1f a5 6a 18 5f 7a 97 92 aa 24 7f 62 fe 5a 35 d5 2a 41 f2
  //   96 c5 59 28 30 61 9a d6 d0 1 da 1d 4f c7 71 13 70 f1 1e d7 65 6 2c e5 98 4c d0 ab a7 7c d5 5c af b8
  //   7a 3 cc bc 9a da e0 54 d dc 94 d 4e 98 9c 2f 5d 47 3e e9 e7 20 14 ce a3 eb f 80 fe d4 c0 aa f9 81 d2
  //   33 52 66 da af e1 57 53 19 45 5e e3 bf bf ce e3 7d 5d 98 1e 2d 5a dc d7 5d c4 c3 10 43 5f 8b 9 ed c9
  //   e3 6 bc de 78 55 12 5d cf 8f 4a cb 55 1d e8 97 b3 fe 11 7e 67 c6 3d 31 90 e9 2a 34 8 39 13 8 b7 ad
  //   21 8c 26 63 22 9f 52 e7 78 a c2 b5 53 9d db fc 22 97 73 a4 46 4a a3 92 8 ff e1 2a cd 16 4d 15 88 71
  //   4a 43 6f 13 50 33 f0 3 ff 72 e6 76 78 60 8 2c e8 39 a1 1a 65 53 85 48 fc a4 43 fc a 87 97 18 ca bf
  //   22 c0 2f bb 5c 3f f4 1b c9 2a f0 73 6a c6 ae 4d 76 a6 3d 74 49 98 43 6f 9c c2 58 4b f6 7 90 9e 62 ae
  //   59 c7 62 45 88 7a 23 c3 ad 7b f1 ec ae a9 ed f9 93 3d fc 77 9e 54 2 6f 9e aa 4f c6 84 a7 59 e7 36 9f
  //   ab 9e a3 56 1d 47 16 c1 45 27 cf 13 2d 19 cf f7 45 6c f3 19 9b b 44 ea 49 de 8d a4 2d 70 2c 8c df d2
  //   2d 76 df be 94 8e e fe f9 54 5f e 5a e8 ce 0 2c 87 90 9f b3 55 8b d7 93 5c 8 54 a6 d4 a6 68 e a4 91
  //   31 8e 28 f4 fa 15 35 ab e1 9b 59 3d ba 30 67 9 33 52 31 be 38 7e 97 10 98 9 c0 a8 e8 2f a7 5b a7 6c
  //   d9 9e a3 a 7c 39 9a fb 93 3b 23 e8 7f 2d ce 89 c8 8a 8a 37 1d 6d 47 be 99 8c dc 78 47 65 29 96 e8 b6
  //   80 c0 f3 31 40 e1 dc 70 c3 3b 99 26 79 c1 61 97 54 a5 b6 49 67 2e a5 fb c9 cf 4c d6 bf 75 9c e2 19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
endmodule

module HalfAdder (
  input  In1,
  input  In2,
  output Carry,
  output Out1
);

  wire or_1_out;

  or or_1 (or_1_out, In1, In2);
  and and_1 (Carry, In2, In1);
  xor xor_1 (Out1, Carry, or_1_out);
endmodule

module FullAdder (
  input  In1,
  input  In2,
  input  CarryIn,
  output Carry,
  output Result
);

  wire and_1_out, halfadder_1_carry, halfadder_1_out1;

  HalfAdder halfadder_1 (.Carry(halfadder_1_carry), .Out1(halfadder_1_out1), .In1(In1), .In2(In2));
  xor xor_1 (Result, CarryIn, halfadder_1_out1);
  or or_1 (Carry, halfadder_1_carry, and_1_out);
  and and_1 (and_1_out, halfadder_1_out1, CarryIn);
endmodule

module EightBitAdder (
  input  CarryIn,
  input  [7:0] in_2,
  input  [7:0] in_3,
  output [7:0] out_4,
  output CarryOut
);

  wire fulladder_1_carry, fulladder_2_carry, fulladder_3_carry, fulladder_4_carry, fulladder_5_carry,
       fulladder_6_carry, fulladder_7_carry;

  FullAdder fulladder_1 (.In1(in_2[0]), .In2(in_3[0]), .CarryIn(CarryIn), .Carry(fulladder_1_carry), .Result(out_4[0]));
  FullAdder fulladder_2 (
    .In1(in_2[1]), .In2(in_3[1]), .CarryIn(fulladder_1_carry), .Carry(fulladder_2_carry), .Result(out_4[1]));
  FullAdder fulladder_3 (
    .In1(in_2[2]), .In2(in_3[2]), .CarryIn(fulladder_2_carry), .Carry(fulladder_3_carry), .Result(out_4[2]));
  FullAdder fulladder_4 (
    .In1(in_2[3]), .In2(in_3[3]), .CarryIn(fulladder_3_carry), .Carry(fulladder_4_carry), .Result(out_4[3]));
  FullAdder fulladder_5 (
    .In1(in_2[4]), .In2(in_3[4]), .CarryIn(fulladder_4_carry), .Carry(fulladder_5_carry), .Result(out_4[4]));
  FullAdder fulladder_6 (
    .In1(in_2[5]), .In2(in_3[5]), .CarryIn(fulladder_5_carry), .Carry(fulladder_6_carry), .Result(out_4[5]));
  FullAdder fulladder_7 (
    .In1(in_2[6]), .In2(in_3[6]), .CarryIn(fulladder_6_carry), .Carry(fulladder_7_carry), .Result(out_4[6]));
  FullAdder fulladder_8 (
    .In1(in_2[7]), .In2(in_3[7]), .CarryIn(fulladder_7_carry), .Carry(CarryOut), .Result(out_4[7]));
endmodule

module LogicGateDeriving (
  input  in_1,
  input  in_2,
  input  in_3,
  input  in_4,
  input  in_5,
  input  in_6,
  input  in_7,
  input  in_8,
  input  in_9,
  input  in_10,
  input  in_11,
  input  in_12,
  input  in_13,
  output out_14,
  output out_15,
  output out_16,
  output out_17,
  output out_18,
  output out_19,
  output out_20
);

  wire nand_2_out, nand_3_out, nand_4_out, nand_5_out, not_3_out, not_5_out, not_6_out, or_1_out, or_2_out,
       xor_1_out;

  or or_1 (or_1_out, in_8, in_9);
  nand nand_1 (out_14, in_1, in_1);
  nand nand_2 (nand_2_out, in_2, in_3);
  nand nand_3 (nand_3_out, in_4, in_6);
  not not_1 (out_18, or_1_out);
  nand nand_4 (nand_4_out, in_10, in_11);
  or or_2 (or_2_out, in_10, in_11);
  xor xor_1 (xor_1_out, in_12, in_13);
  not not_2 (out_15, nand_2_out);
  not not_3 (not_3_out, in_4);
  nand nand_5 (nand_5_out, nand_3_out, in_6);
  not not_4 (out_20, xor_1_out);
  and and_1 (out_19, nand_4_out, or_2_out);
  nand nand_6 (out_16, not_3_out, nand_5_out);
  not not_5 (not_5_out, in_5);
  not not_6 (not_6_out, in_7);
  nand nand_7 (out_17, not_5_out, not_6_out);
endmodule

module MyMultiplexer (
  input  Input1,
  input  Input2,
  input  Selecter,
  output Output1
);

  wire and_1_out, and_2_out;

  and and_1 (and_1_out, ~Selecter, Input1);  // AND_Gate
  and and_2 (and_2_out, Input2, Selecter);
  xor xor_1 (Output1, and_1_out, and_2_out);
endmodule

module FourBitMultiplexer (
  input  Input0,
  input  Input1,
  input  Input2,
  input  Input3,
  input  [1:0] Selecter,
  output Output1
);

  wire mymultiplexer_1_output1, mymultiplexer_2_output1;

  J_K_Flip_Flop j_k_ff_1 ();  // open: J, clk, K, Q, Qn, preset, reset
  MyMultiplexer mymultiplexer_1 (
    .Output1(mymultiplexer_1_output1), .Input1(Input0), .Input2(Input1), .Selecter(Selecter[0]));
  MyMultiplexer mymultiplexer_2 (
    .Output1(mymultiplexer_2_output1), .Input1(Input2), .Input2(Input3), .Selecter(Selecter[0]));
  MyMultiplexer mymultiplexer_3 (
    .Output1(Output1), .Input1(mymultiplexer_1_output1), .Input2(mymultiplexer_2_output1),
    .Selecter(Selecter[1]));
endmodule

module MyDemultiplexer (
  input  Input1,
  input  Selecter,
  output Output0,
  output Output1
);

  and and_1 (Output0, ~Selecter, Input1);  // AND_Gate
  and and_2 (Output1, Input1, Selecter);
endmodule
